# Fritzing sketch Steckplan_V1_Paganini (saved by Fritzing 1.0.1rc)
breadboards: 1

parts:
  Arduino = Arduino Nano (Rev3.0)
  Button_3 = Pushbutton [package="[THT]"]
  Button_2 = Pushbutton [package="[THT]"]
  Button_1 = Pushbutton [package="[THT]"]
  LED1 = RGB LED (com. cathode, rbg) [package="5 mm [THT]"]
  Part2 = Adafruit BME680 [part_number="Adafruit #3660"]
  R1 = Resistor [tolerance=±5% resistance=220 package="2010 [SMD]"]
  R2 = Resistor [tolerance=±5% resistance=100 package="2010 [SMD]"]
  R3 = Resistor [tolerance=±5% resistance=100 package="2010 [SMD]"]
  Grove1 = Grove OLED 128x96

nets:
  GND: Arduino.GND, Button_3.Pin_3, Button_3.Pin_4, Button_2.Pin_3, Button_2.Pin_4, Button_1.Pin_3, Button_1.Pin_4, LED1.common_cathode, Part2.GND, Grove1.GND
  N1: Arduino.D2, Button_3.Pin_1, Button_3.Pin_2
  N2: Arduino.D3, Button_2.Pin_1, Button_2.Pin_2
  N3: Arduino.D4, Button_1.Pin_1, Button_1.Pin_2
  N4: Arduino.A7, R3.Pin_1
  N5: Arduino.A6, R2.Pin_1
  N6: Arduino.A5, Part2.SCK/SCL, Grove1.SCL
  N7: Arduino.A4, Part2.SDI/SDA, Grove1.SDA
  N8: Arduino.A0, R1.Pin_1
  VCC: Arduino.3V3, Part2.VCC, Grove1.VCC
  N9: LED1.red_anode, R1.Pin_0
  N10: LED1.blue_anode, R2.Pin_0
  N11: LED1.green_anode, R3.Pin_0
