# Fritzing sketch steckplatinendesign_v1_maria (saved by Fritzing 0.9.6b)
breadboards: 1

parts:
  R1 = Resistor [tolerance=±5% resistance=220 package="1206 [SMD]"]
  R2 = Resistor [tolerance=±5% resistance=220 package="1206 [SMD]"]
  R3 = Resistor [tolerance=±5% resistance=220 package="1206 [SMD]"]
  LED1 = RGB LED (com. cathode, rgb) [package="5 mm [THT]"]
  S1 = Pushbutton [package="[THT]"]
  Grove1 = Grove OLED 128x96
  Part2 = Altitude/Pressure Sensor - MPL3115A2 Breakout [part_number=SEN-11084]
  S2 = Pushbutton [package="[THT]"]
  S3 = Pushbutton [package="[THT]"]
  Part1 = Arduino Nano (Rev3.0) (ICSP)

nets:
  N1: R1.Pin_0, LED1.red_anode
  N2: R1.Pin_1, Part1.A0
  N3: R2.Pin_0, LED1.green_anode
  N4: R2.Pin_1, Part1.A1
  N5: R3.Pin_0, LED1.blue_anode
  N6: R3.Pin_1, Part1.A2
  GND: LED1.common_cathode, S1.Pin_3, S1.Pin_4, Grove1.GND, Part2.GND, S2.Pin_3, S2.Pin_4, S3.Pin_3, S3.Pin_4, Part1.GND
  N7: S1.Pin_1, S1.Pin_2, Part1.D2
  VCC: Grove1.VCC, Part2.VCC, Part1.3V3
  N8: Grove1.SDA, Part2.SDA, Part1.A4
  N9: Grove1.SCL, Part2.SCL, Part1.A5
  N10: S2.Pin_1, S2.Pin_2, Part1.D7
  N11: S3.Pin_1, S3.Pin_2, Part1.D8
